# Fritzing sketch RPi_weathershield (saved by Fritzing 0.9.2b)

parts:
  Part_1 = Weather Shield [part_number=DEV-12081]
  Raspberry_Pi1 = Raspberry Pi 2

nets:
  GND: Part_1.D5, Part_1.GND, Raspberry_Pi1.GND
  N1: Part_1.D8, Raspberry_Pi1.GPIO5
  N2: Part_1.D9, Raspberry_Pi1.GPIO6
  N3: Part_1.SDA, Raspberry_Pi1.GPIO2
  N4: Part_1.SCL, Raspberry_Pi1.GPIO3
  VIN: Part_1.VIN, Raspberry_Pi1.5V
  5V: Part_1.5V, Raspberry_Pi1.3v3

custom parts:
  Weather Shield: Weather Shield includes: - ALS-PT19 Light Sensor - HTU21D Humidity Sensor - MPL3115A2 - TEMT6000 Check out the product page on www.sparkfun.com for documentation!
