# Fritzing sketch 16x2LCDDiagram (saved by Fritzing 0.8.7b)
breadboards: 1

parts:
  LCD1 = LCD screen
  Intel(R)_Galileo_1 = Intel(R) Galileo
  R1 = Resistor [package="2010 [SMD]"]

nets:
  VSS: LCD1.VSS, LCD1.R/W, LCD1.LED-, Intel(R)_Galileo_1.GND, R1.Pin_1
  VDD: LCD1.VDD, LCD1.LED+, Intel(R)_Galileo_1.3V3
  N1: LCD1.V0, R1.Pin_0
  N2: LCD1.RS, Intel(R)_Galileo_1.D4
  N3: LCD1.E, Intel(R)_Galileo_1.D5_PWM
  N4: LCD1.DB4, Intel(R)_Galileo_1.D6_PWM
  N5: LCD1.DB5, Intel(R)_Galileo_1.D7
  N6: LCD1.DB6, Intel(R)_Galileo_1.D8
  N7: LCD1.DB7, Intel(R)_Galileo_1.D9_PWM

custom parts:
  Intel(R) Galileo: Galileo is a microcontroller board based on the Intel® Quark SoC X1000 Application Processor, a 32-bit Intel Pentium-class system on a chip (datasheet). It’s the first board based on Intel® architecture designed to be hardware and software pin-compatible with Arduino shields designed for the Uno R3. Digital pins 0 to 13 (and the adjacent AREF and GND pins), Analog inputs 0 to 5, the power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
