# Fritzing sketch DB_Accelerometer_SPI (saved by Fritzing 0.9.2b)

parts:
  J1 = female pin header, 20 pins [form="♀ (female)"]
  Part2 = Triple Axis Accelerometer Breakout - ADXL345
  part = SparkFun Voltage-Level Translator Breakout - TXB0104
  J2 = female pin header, 20 pins [form="♀ (female)"]

nets:
  N1: J1.pin18, part.VCCA
  N2: J1.pin19, Part2.VCC, part.VCCB
  N3: Part2.GND, part.GND#12
  N4: Part2.CS, part.B4
  N5: Part2.SDO, part.B3
  N6: Part2.SDA, part.B2
  N7: Part2.SCL, part.B1
  N8: part.A1, J2.pin4
  N9: part.A2, J2.pin7
  N10: part.A3, J2.pin5
  N11: part.A4, J2.pin6
  N12: part.GND#13, J2.pin20

notes:
  Pin 1
  Pin 2
  Pin 40
  Pin 39

custom parts:
  SparkFun Voltage-Level Translator Breakout - TXB0104: This is a breakout board for the Texas Instruments TXB0104 module. The TXB0104 is a 4-bit bidirectional voltage-level translator with automatic direction sensing. This 4-bit noninverting translator uses two separate configurable power-supply rails. The A port is designed to track VCCA. VCCA accepts any supply voltage from 1.2V to 3.6V. The B port is designed to track VCCB. VCCB accepts any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
