# Fritzing sketch DB_Blinky (saved by Fritzing 0.9.2b)
breadboards: 1

parts:
  R1 = Resistor [tolerance=±5% resistance=330 package=THT]
  J1 = female pin header, 20 pins [form="♀ (female)"]
  J2 = female pin header, 20 pins [form="♀ (female)"]
  LED1 = smd LED [color="Red (633nm)" package="0805 [SMD]"]

nets:
  N1: R1.Pin_0, J1.pin18
  N2: R1.Pin_1, LED1.anode
  N3: J2.pin12, LED1.cathode

notes:
  Pin 1
  Pin 2
  Pin 40
  Pin 35
  Pin 24
