# Fritzing sketch DB_Display_SPI (saved by Fritzing 0.9.2b)
breadboards: 1

parts:
  J1 = female pin header, 20 pins [form="♀ (female)"]
  J2 = female pin header, 20 pins [form="♀ (female)"]
  BB1 = 8-Line Bi-Directional Level Shifter
  OLED2 = 128x64 Monochrom OLED Display with SPI Control

nets:
  N1: J1.pin18, BB1.no_name_yet#1
  N2: J1.pin19, BB1.no_name_yet#11, OLED2.Vin
  N3: J2.pin5, BB1.no_name_yet#5
  N4: J2.pin6, BB1.no_name_yet#2
  N5: J2.pin7, BB1.no_name_yet#6
  N6: J2.pin12, BB1.no_name_yet#4
  N7: J2.pin13, BB1.no_name_yet#3
  N8: J2.pin20, BB1.no_name_yet#20, OLED2.GND
  N9: BB1.no_name_yet#12, OLED2.CS
  N10: BB1.no_name_yet#13, OLED2.Reset
  N11: BB1.no_name_yet#14, OLED2.SA0/DC
  N12: BB1.no_name_yet#15, OLED2.Clock
  N13: BB1.no_name_yet#16, OLED2.Data

notes:
  Pin 1
  Pin 2
  Pin 40
  Pin 39

custom parts:
  8-Line Bi-Directional Level Shifter: 8-channel Bi-Directional Level Shifter with TXB0108
