# Fritzing sketch MBM_potentiometer3208 (saved by Fritzing 0.9.2b)
breadboards: 1

parts:
  J3 = male pin header, 13 pins [form="♂ (male)"]
  J4 = male pin header, 13 pins [form="♂ (male)"]
  R2 = Resistor [tolerance=±5% resistance=330 package=THT]
  LED1 = LED - 5mm [color="Red (633nm)" package="5 mm [THT]"]
  R3 = TRIMPOT [package=3362u-2]
  IC1 = DIP - 16 pins [chip_label=MCP3208 package="DIP (Dual Inline) [THT]"]

nets:
  N1: J3.pin12, R2.Pin_1, R3.CCW, IC1.Vref, IC1.Vdd
  N2: J4.pin8, IC1.CLC
  N3: J4.pin9, IC1.Din_MOSI
  N4: J4.pin10, IC1.Dout_MISO
  N5: J4.pin11, IC1.CS
  N6: J4.pin13, LED1.cathode, R3.CW, IC1.DGND, IC1.AGN
  N7: R2.Pin_0, LED1.anode
  N8: R3.WIPER, IC1.Chan0

notes:
  MBM Header
  1
  26

custom parts:
  DIP - 16 pins: A DIP stand-in part for whatever IC you want. With 16 pins on a 300mil dual inline package (DIP) footprint.
