# Fritzing sketch RPi_lcd_screen (saved by Fritzing 0.9.2b)
breadboards: 1

parts:
  R1 = Rotary Potentiometer (Small) [maximum_resistance=100kΩ package=THT]
  LCD1 = LCD screen
  Raspberry_Pi1 = Raspberry Pi 2
  R2 = Resistor [tolerance=±5% resistance=220 package=THT]

nets:
  VSS: R1.leg1, LCD1.VSS, LCD1.R/W, LCD1.LED-, Raspberry_Pi1.GND
  N1: R1.wiper, LCD1.V0
  VDD: R1.leg2, LCD1.VDD, Raspberry_Pi1.5V, R2.Pin_1
  N2: LCD1.RS, Raspberry_Pi1.GPIO20
  N3: LCD1.E, Raspberry_Pi1.GPIO16
  N4: LCD1.DB4, Raspberry_Pi1.GPIO2
  N5: LCD1.DB5, Raspberry_Pi1.GPIO3
  N6: LCD1.DB6, Raspberry_Pi1.GPIO4
  N7: LCD1.DB7, Raspberry_Pi1.GPIO17
  N8: LCD1.LED+, R2.Pin_0
